# Fritzing sketch Mode0Damper (saved by Fritzing 0.9.3b)
circuit board: 10.2917cm x 7.30014cm
breadboards: 1

parts:
  IC1 = IC, DIP package, 8 pins [chip_label=IC]
  IC2 = IC, DIP package, 8 pins [chip_label=IC]
  R11 = Resistor [tolerance=±5% resistance=10k package=THT]
  IC3 = IC, DIP package, 8 pins [chip_label=IC]
  R12 = Resistor [tolerance=±5% resistance=330k package=THT]
  R13 = Resistor [tolerance=±5% resistance=1M package=THT]
  IC4 = IC, DIP package, 8 pins [chip_label=IC]
  R14 = Resistor [tolerance=±5% resistance=10k package=THT]
  R15 = Resistor [tolerance=±5% resistance=330k package=THT]
  R16 = Resistor [tolerance=±5% resistance=1M package=THT]
  Teensy1 = Teensy 3.6 (Basic)
  C3 = Ceramic Capacitor [capacitance=1µF package="100 mil [THT, multilayer]"]
  C4 = Ceramic Capacitor [capacitance=1µF package="100 mil [THT, multilayer]"]
  R17 = Resistor [tolerance=±5% resistance=10k package=THT]
  R18 = Resistor [tolerance=±5% resistance=10k package=THT]
  IC5 = Voltage Regulator [package=to-220-alt]
  IC6 = Voltage Regulator [package=78xxl]
  C5 = Ceramic Capacitor [capacitance=1µF package="100 mil [THT, multilayer]"]
  C6 = Ceramic Capacitor [capacitance=1µF package="100 mil [THT, multilayer]"]
  C7 = Ceramic Capacitor [capacitance=1µF package="100 mil [THT, multilayer]"]
  C8 = Ceramic Capacitor [capacitance=1µF package="100 mil [THT, multilayer]"]
  C10 = Ceramic Capacitor [capacitance=1µF package="100 mil [THT, multilayer]"]
  C11 = Ceramic Capacitor [capacitance=1µF package="100 mil [THT, multilayer]"]
  R22 = Resistor [tolerance=±5% resistance=15k package=THT]
  R3 = Resistor [tolerance=±5% resistance=22k package=THT]
  R8 = Resistor [tolerance=±5% resistance=22k package=THT]
  R20 = Resistor [tolerance=±5% resistance=15k package=THT]
  R6 = Resistor [tolerance=±5% resistance=22k package=THT]
  R9 = Resistor [tolerance=±5% resistance=22k package=THT]
  R21 = Resistor [tolerance=±5% resistance=3.3k package=THT]
  R19 = Resistor [tolerance=±5% resistance=3.3k package=THT]
  R7 = Resistor [tolerance=±5% resistance=330k package=THT]
  R10 = Resistor [tolerance=±5% resistance=330k package=THT]

nets:
  N1: IC1.pin2, R3.Pin_1, R6.Pin_1, R7.Pin_1
  GND: IC1.pin3, IC2.pin3, IC3.pin3, IC4.pin3, Teensy1.GND, Teensy1.AGND, Teensy1.GND1, R17.Pin_0, R18.Pin_1, IC5.GND, IC6.GND, C5.0, C6.1, C7.0, C8.0, R21.Pin_0, R19.Pin_0
  N2: IC1.pin4, IC2.pin4, IC3.pin4, R13.Pin_0, IC4.pin4, R16.Pin_0, IC5.OUT, C7.1, R7.Pin_0, R10.Pin_0
  N3: IC1.pin6, R6.Pin_0
  N4: IC1.pin7, IC2.pin7, IC3.pin7, IC4.pin7, IC6.OUT, C8.1
  N5: IC2.pin2, R8.Pin_1, R9.Pin_1, R10.Pin_1
  N6: IC2.pin6, R9.Pin_0
  N7: R11.Pin_0, C3.0, C11.0
  N8: R11.Pin_1, IC3.pin2, R12.Pin_1, R13.Pin_1
  N9: IC3.pin6, R12.Pin_0, Teensy1.A0/D14
  N10: IC4.pin2, R14.Pin_0, R15.Pin_1, R16.Pin_1
  N11: IC4.pin6, R15.Pin_0, Teensy1.A3/D17
  N12: R14.Pin_1, C4.0, C10.0
  N13: Teensy1.3V3, Teensy1.3V3_1
  N14: Teensy1.A21/DAC0, R22.Pin_1
  N15: Teensy1.A22/DAC1, R20.Pin_1
  N16: C3.1, C11.1
  N17: C4.1, C10.1
  N18: R17.Pin_1, IC6.IN, C6.0
  N19: R18.Pin_0, IC5.IN, C5.1
  N20: R22.Pin_0, R3.Pin_0, R21.Pin_1
  N21: R8.Pin_0, R20.Pin_0, R19.Pin_1

custom parts:
  Teensy 3.6 (Basic): The Teensy is a complete USB-based microcontoller development system, in a very small footprint, capable of implementing many types of projects. All programming is done via the USB port. No special programmer is needed, only a standard micro-USB cable and a PC or Macintosh with a USB port.
